// Logisim project Projeto-Sistemas_Digitais.circ as structural Verilog
module Mux___2_Canais (
  input  Canal_1,
  input  Canal_2,
  input  A,
  output out_4
);

  wire and_1_out, and_2_out;

  and and_1 (and_1_out, Canal_1, ~A);  // AND_Gate
  and and_2 (and_2_out, Canal_2, A);
  or or_1 (out_4, and_1_out, and_2_out);
endmodule

module Mux___16_Canais (
  input  Canal_0,
  input  Canal_1,
  input  Canal_2,
  input  Canal_3,
  input  Canal_4,
  input  Canal_5,
  input  Canal_6,
  input  Canal_7,
  input  Canal_8,
  input  Canal_9,
  input  Canal_10,
  input  Canal_11,
  input  Canal_12,
  input  Canal_13,
  input  Canal_14,
  input  Canal_15,
  input  A,
  input  B,
  input  C,
  input  D,
  output \Saída 
);

  wire and_1_out, and_2_out, and_3_out, and_4_out, and_5_out, and_6_out, and_7_out, and_8_out, and_9_out,
       and_10_out, and_11_out, and_12_out, and_13_out, and_14_out, and_15_out, and_16_out;

  and and_1 (and_1_out, Canal_0, ~A, ~B, ~C, ~D);  // AND_Gate
  and and_2 (and_2_out, Canal_1, ~A, ~B, ~C, D);  // AND_Gate
  and and_3 (and_3_out, Canal_2, ~A, ~B, C, ~D);  // AND_Gate
  and and_4 (and_4_out, Canal_3, ~A, ~B, C, D);  // AND_Gate
  and and_5 (and_5_out, Canal_4, ~A, B, ~C, ~D);  // AND_Gate
  and and_6 (and_6_out, Canal_5, ~A, B, ~C, D);  // AND_Gate
  and and_7 (and_7_out, Canal_6, ~A, B, C, ~D);  // AND_Gate
  and and_8 (and_8_out, Canal_7, ~A, B, C, D);  // AND_Gate
  and and_9 (and_9_out, Canal_8, A, ~B, ~C, ~D);  // AND_Gate
  and and_10 (and_10_out, Canal_9, A, ~B, ~C, D);  // AND_Gate
  and and_11 (and_11_out, Canal_10, A, ~B, C, ~D);  // AND_Gate
  and and_12 (and_12_out, Canal_11, A, ~B, C, D);  // AND_Gate
  and and_13 (and_13_out, Canal_12, A, B, ~C, ~D);  // AND_Gate
  and and_14 (and_14_out, Canal_13, A, B, ~C, D);  // AND_Gate
  and and_15 (and_15_out, Canal_14, A, B, C, ~D);  // AND_Gate
  and and_16 (and_16_out, Canal_15, A, B, C, D);
  or or_1 (\Saída , and_1_out, and_2_out, and_3_out, and_4_out, and_5_out, and_6_out, and_7_out, and_8_out, and_9_out, and_10_out, and_11_out, and_12_out, and_13_out, and_14_out, and_15_out, and_16_out);
endmodule

// MUX 32
module Mux___32_Canais (
  input  Canal_0,
  input  Canal_1,
  input  Canal_2,
  input  Canal_3,
  input  Canal_4,
  input  Canal_5,
  input  Canal_6,
  input  Canal_7,
  input  Canal_8,
  input  Canal_9,
  input  Canal_10,
  input  Canal_11,
  input  Canal_12,
  input  Canal_13,
  input  Canal_14,
  input  Canal_15,
  input  Canal_16,
  input  Canal_17,
  input  Canal_18,
  input  Canal_19,
  input  Canal_20,
  input  Canal_21,
  input  Canal_22,
  input  Canal_23,
  input  Canal_24,
  input  Canal_25,
  input  Canal_26,
  input  Canal_27,
  input  Canal_28,
  input  Canal_29,
  input  Canal_30,
  input  Canal_31,
  input  A,
  input  B,
  input  C,
  input  D,
  input  E,
  output out_38
);

  wire \mux_16_canais_1_saída , \mux_16_canais_2_saída ;

  Mux___16_Canais mux_16_canais_1 (
    .Canal_0(Canal_0), .Canal_1(Canal_1), .Canal_2(Canal_2), .Canal_3(Canal_3), .Canal_4(Canal_4),
    .Canal_5(Canal_5), .Canal_6(Canal_6), .Canal_7(Canal_7), .Canal_8(Canal_8), .Canal_9(Canal_9),
    .Canal_10(Canal_10), .Canal_11(Canal_11), .Canal_12(Canal_12), .Canal_13(Canal_13), .Canal_14(Canal_14),
    .Canal_15(Canal_15), .A(B), .B(C), .C(D), .D(E), .\Saída (\mux_16_canais_1_saída ));
  Mux___16_Canais mux_16_canais_2 (
    .Canal_0(Canal_16), .Canal_1(Canal_17), .Canal_2(Canal_18), .Canal_3(Canal_19), .Canal_4(Canal_20),
    .Canal_5(Canal_21), .Canal_6(Canal_22), .Canal_7(Canal_23), .Canal_8(Canal_24), .Canal_9(Canal_25),
    .Canal_10(Canal_26), .Canal_11(Canal_27), .Canal_12(Canal_28), .Canal_13(Canal_29), .Canal_14(Canal_30),
    .Canal_15(Canal_31), .A(B), .B(C), .C(D), .D(E), .\Saída (\mux_16_canais_2_saída ));
  Mux___2_Canais Mux___2_Canais (
    .Canal_1(\mux_16_canais_1_saída ), .Canal_2(\mux_16_canais_2_saída ), .A(A), .out_4(out_38));
endmodule

// Full Adder
module Somador_Completo (
  input  A,
  input  B,
  input  Carry_In,
  output Sum,
  output Carry_Out
);

  wire and_1_out, and_2_out, and_3_out, xor_1_out;

  xor xor_1 (xor_1_out, A, B);
  and and_1 (and_1_out, A, B);
  and and_2 (and_2_out, A, Carry_In);
  and and_3 (and_3_out, B, Carry_In);
  xor xor_2 (Sum, xor_1_out, Carry_In);
  or or_1 (Carry_Out, and_1_out, and_2_out, and_3_out);
endmodule

// Full subtractor
module Subtrator_Completo (
  input  A,
  input  B,
  input  Carry_In,
  output Subtraction,
  output Carry_Out
);

  wire and_1_out, and_2_out, and_3_out, xor_1_out;

  xor xor_1 (xor_1_out, A, B);
  and and_1 (and_1_out, ~A, B);  // AND_Gate
  and and_2 (and_2_out, ~A, Carry_In);  // AND_Gate
  and and_3 (and_3_out, B, Carry_In);
  xor xor_2 (Subtraction, xor_1_out, Carry_In);
  or or_1 (Carry_Out, and_1_out, and_2_out, and_3_out);
endmodule

module ULACell (
  input  A,
  input  B,
  input  Vem_1,
  input  [4:0] OperCode,
  output Resultado,
  output Vai_1
);

  wire and_1_out, nand_1_out, or_1_out, somador_completo_1_sum, xor_1_out;

  and and_1 (and_1_out, A, B);
  or or_1 (or_1_out, A, B);
  xor xor_1 (xor_1_out, A, B);
  Somador_Completo somador_completo_1 (.A(A), .B(B), .Carry_In(Vem_1), .Sum(somador_completo_1_sum), .Carry_Out(Vai_1));
  nand nand_1 (nand_1_out, A, B);
  \Menu_de_Operações  \menu_de_operações_1  ();
  Mux___32_Canais mux_32_canais_1 (
    .Canal_0(and_1_out), .Canal_1(or_1_out), .Canal_2(xor_1_out), .Canal_3(somador_completo_1_sum),
    .Canal_4(B), .Canal_5(B), .Canal_6(B), .Canal_7(A), .Canal_8(B), .Canal_9(nand_1_out),
    .out_38(Resultado), .B(OperCode[3]), .C(OperCode[2]), .D(OperCode[1]), .E(OperCode[0]), .A(OperCode[4]));  // open: Canal_10, Canal_11, Canal_12, Canal_13, Canal_14, Canal_15, Canal_16, Canal_17, Canal_18, Canal_19, Canal_20, Canal_21, Canal_22, Canal_23, Canal_24, Canal_25, Canal_26, Canal_27, Canal_28, Canal_29, Canal_30, Canal_31
endmodule

module \ULA___32_Bits__2_Números  (
  input  [31:0] A,
  input  [4:0] SA,
  input  [31:0] B,
  input  [4:0] OperCode,
  output [31:0] \Saída ,
  output Overflow
);

  wire A0, A1, A2, A3, A4, A5, A6, A7, A8, A9, A10, A11, A12, A13, A14, A15, A16, A17, A18, A19, A20, A21,
       A22, A23, A24, A25, A26, A27, A28, A29, A30, A31, B0, B1, B2, B3, B4, B5, B6, B7, B8, B9, B10, B11,
       B12, B13, B14, B15, B16, B17, B18, B19, B20, B21, B22, B23, B24, B25, B26, B27, B28, B29, B30, B31,
       \lua_detect_1_saída , \sll_32_detect_1_saída , \sll_detect_1_saída , \sra_detect_1_saída ,
       \srl_detect_1_saída , ulacell_1_vai_1, ulacell_2_vai_1, ulacell_3_vai_1, ulacell_4_vai_1,
       ulacell_5_vai_1, ulacell_6_vai_1, ulacell_7_vai_1, ulacell_8_vai_1, ulacell_9_vai_1, ulacell_10_vai_1,
       ulacell_11_vai_1, ulacell_12_vai_1, ulacell_13_vai_1, ulacell_14_vai_1, ulacell_15_vai_1,
       ulacell_16_vai_1, ulacell_17_vai_1, ulacell_18_vai_1, ulacell_19_vai_1, ulacell_20_vai_1,
       ulacell_21_vai_1, ulacell_22_vai_1, ulacell_23_vai_1, ulacell_24_vai_1, ulacell_25_vai_1,
       ulacell_26_vai_1, ulacell_27_vai_1, ulacell_28_vai_1, ulacell_29_vai_1, ulacell_30_vai_1,
       ulacell_31_vai_1;
  wire [31:0] \shift_left_logical_deslocar_à_esquerda_1_saída ,
       \shift_right_logical_deslocar_à_direita_1_saída , \sll_32_1_saída ;

  ULACell ulacell_1 (
    .Vem_1(ulacell_3_vai_1), .Resultado(\Saída [15]), .Vai_1(ulacell_1_vai_1), .A(A15), .B(B15),
    .OperCode(OperCode));
  ULACell ulacell_2 (
    .Vem_1(ulacell_1_vai_1), .Resultado(\Saída [16]), .Vai_1(ulacell_2_vai_1), .A(A16), .B(B16),
    .OperCode(OperCode));
  \Operação_LUA  \operação_lua_1  (
    .Entrada(A), .OperCode(\lua_detect_1_saída ),
    .\Saída ({A31, A30, A29, A28, A27, A26, A25, A24, A23, A22, A21, A20, A19, A18, A17, A16, A15, A14, A13, A12, A11, A10, A9, A8, A7, A6, A5, A4, A3, A2, A1, A0}));
  LUA_Detect lua_detect_1 (.\Saída (\lua_detect_1_saída ), .OperCode(OperCode));
  ULACell ulacell_3 (
    .Vem_1(ulacell_5_vai_1), .Resultado(\Saída [14]), .Vai_1(ulacell_3_vai_1), .A(A14), .B(B14),
    .OperCode(OperCode));
  ULACell ulacell_4 (
    .Vem_1(ulacell_2_vai_1), .Resultado(\Saída [17]), .Vai_1(ulacell_4_vai_1), .A(A17), .B(B17),
    .OperCode(OperCode));
  ULACell ulacell_5 (
    .Vem_1(ulacell_7_vai_1), .Resultado(\Saída [13]), .Vai_1(ulacell_5_vai_1), .A(A13), .B(B13),
    .OperCode(OperCode));
  ULACell ulacell_6 (
    .Vem_1(ulacell_4_vai_1), .Resultado(\Saída [18]), .Vai_1(ulacell_6_vai_1), .A(A18), .B(B18),
    .OperCode(OperCode));
  ULACell ulacell_7 (
    .Vem_1(ulacell_9_vai_1), .Resultado(\Saída [12]), .Vai_1(ulacell_7_vai_1), .A(A12), .B(B12),
    .OperCode(OperCode));
  ULACell ulacell_8 (
    .Vem_1(ulacell_6_vai_1), .Resultado(\Saída [19]), .Vai_1(ulacell_8_vai_1), .A(A19), .B(B19),
    .OperCode(OperCode));
  ULACell ulacell_9 (
    .Vem_1(ulacell_11_vai_1), .Resultado(\Saída [11]), .Vai_1(ulacell_9_vai_1), .A(A11), .B(B11),
    .OperCode(OperCode));
  ULACell ulacell_10 (
    .Vem_1(ulacell_8_vai_1), .Resultado(\Saída [20]), .Vai_1(ulacell_10_vai_1), .A(A20), .B(B20),
    .OperCode(OperCode));
  SLL___32 sll_32_1 (.Entrada(B), .\Saída (\sll_32_1_saída ), .SA(SA), .SLL_Detect__New(\sll_32_detect_1_saída ));
  SLL_32___Detect sll_32_detect_1 (.\Saída (\sll_32_detect_1_saída ), .OperCode(OperCode));
  SRL_Detect srl_detect_1 (.\Saída (\srl_detect_1_saída ), .OperCode(OperCode));
  ULACell ulacell_11 (
    .Vem_1(ulacell_13_vai_1), .Resultado(\Saída [10]), .Vai_1(ulacell_11_vai_1), .A(A10), .B(B10),
    .OperCode(OperCode));
  ULACell ulacell_12 (
    .Vem_1(ulacell_10_vai_1), .Resultado(\Saída [21]), .Vai_1(ulacell_12_vai_1), .A(A21), .B(B21),
    .OperCode(OperCode));
  \Shift_Right_Logical__Deslocar_à_Direita  \shift_right_logical_deslocar_à_direita_1  (
    .Entrada(\sll_32_1_saída ), .OperCode(\srl_detect_1_saída ),
    .\Saída (\shift_right_logical_deslocar_à_direita_1_saída ));
  \Shift_Left_Logical__Deslocar_à_Esquerda  \shift_left_logical_deslocar_à_esquerda_1  (
    .Entrada(\shift_right_logical_deslocar_à_direita_1_saída ), .OperCode(\sll_detect_1_saída ),
    .\Saída (\shift_left_logical_deslocar_à_esquerda_1_saída ));
  SLL_Detect sll_detect_1 (.\Saída (\sll_detect_1_saída ), .OperCode(OperCode));
  SRA_Detect sra_detect_1 (.\Saída (\sra_detect_1_saída ), .OperCode(OperCode));
  ULACell ulacell_13 (
    .Vem_1(ulacell_15_vai_1), .Resultado(\Saída [9]), .Vai_1(ulacell_13_vai_1), .A(A9), .B(B9),
    .OperCode(OperCode));
  ULACell ulacell_14 (
    .Vem_1(ulacell_12_vai_1), .Resultado(\Saída [22]), .Vai_1(ulacell_14_vai_1), .A(A22), .B(B22),
    .OperCode(OperCode));
  \Shift_Right_Arithmetic__Deslocamento_Aritmético_à_Direita  \shift_right_arithmetic_deslocamento_aritmético_à_direita_1  (
    .Entrada(\shift_left_logical_deslocar_à_esquerda_1_saída ), .OperCode(\sra_detect_1_saída ),
    .\Saída ({B31, B30, B29, B28, B27, B26, B25, B24, B23, B22, B21, B20, B19, B18, B17, B16, B15, B14, B13, B12, B11, B10, B9, B8, B7, B6, B5, B4, B3, B2, B1, B0}));
  ULACell ulacell_15 (
    .Vem_1(ulacell_17_vai_1), .Resultado(\Saída [8]), .Vai_1(ulacell_15_vai_1), .A(A8), .B(B8),
    .OperCode(OperCode));
  ULACell ulacell_16 (
    .Vem_1(ulacell_14_vai_1), .Resultado(\Saída [23]), .Vai_1(ulacell_16_vai_1), .A(A23), .B(B23),
    .OperCode(OperCode));
  ULACell ulacell_17 (
    .Vem_1(ulacell_19_vai_1), .Resultado(\Saída [7]), .Vai_1(ulacell_17_vai_1), .A(A7), .B(B7),
    .OperCode(OperCode));
  ULACell ulacell_18 (
    .Vem_1(ulacell_16_vai_1), .Resultado(\Saída [24]), .Vai_1(ulacell_18_vai_1), .A(A24), .B(B24),
    .OperCode(OperCode));
  ULACell ulacell_19 (
    .Vem_1(ulacell_21_vai_1), .Resultado(\Saída [6]), .Vai_1(ulacell_19_vai_1), .A(A6), .B(B6),
    .OperCode(OperCode));
  ULACell ulacell_20 (
    .Vem_1(ulacell_18_vai_1), .Resultado(\Saída [25]), .Vai_1(ulacell_20_vai_1), .A(A25), .B(B25),
    .OperCode(OperCode));
  ULACell ulacell_21 (
    .Vem_1(ulacell_23_vai_1), .Resultado(\Saída [5]), .Vai_1(ulacell_21_vai_1), .A(A5), .B(B5),
    .OperCode(OperCode));
  ULACell ulacell_22 (
    .Vem_1(ulacell_20_vai_1), .Resultado(\Saída [26]), .Vai_1(ulacell_22_vai_1), .A(A26), .B(B26),
    .OperCode(OperCode));
  ULACell ulacell_23 (
    .Vem_1(ulacell_25_vai_1), .Resultado(\Saída [4]), .Vai_1(ulacell_23_vai_1), .A(A4), .B(B4),
    .OperCode(OperCode));
  ULACell ulacell_24 (
    .Vem_1(ulacell_22_vai_1), .Resultado(\Saída [27]), .Vai_1(ulacell_24_vai_1), .A(A27), .B(B27),
    .OperCode(OperCode));
  ULACell ulacell_25 (
    .Vem_1(ulacell_27_vai_1), .Resultado(\Saída [3]), .Vai_1(ulacell_25_vai_1), .A(A3), .B(B3),
    .OperCode(OperCode));
  ULACell ulacell_26 (
    .Vem_1(ulacell_24_vai_1), .Resultado(\Saída [28]), .Vai_1(ulacell_26_vai_1), .A(A28), .B(B28),
    .OperCode(OperCode));
  ULACell ulacell_27 (
    .Vem_1(ulacell_28_vai_1), .Resultado(\Saída [2]), .Vai_1(ulacell_27_vai_1), .A(A2), .B(B2),
    .OperCode(OperCode));
  ULACell ulacell_28 (
    .Vem_1(ulacell_31_vai_1), .Resultado(\Saída [1]), .Vai_1(ulacell_28_vai_1), .A(A1), .B(B1),
    .OperCode(OperCode));
  ULACell ulacell_29 (
    .Vem_1(ulacell_26_vai_1), .Resultado(\Saída [29]), .Vai_1(ulacell_29_vai_1), .A(A29), .B(B29),
    .OperCode(OperCode));
  ULACell ulacell_30 (
    .Vem_1(ulacell_29_vai_1), .Resultado(\Saída [30]), .Vai_1(ulacell_30_vai_1), .A(A30), .B(B30),
    .OperCode(OperCode));
  ULACell ulacell_31 (
    .Vem_1(1'b0), .Resultado(\Saída [0]), .Vai_1(ulacell_31_vai_1), .A(A0), .B(B0), .OperCode(OperCode));
  ULACell ulacell_32 (
    .Vem_1(ulacell_30_vai_1), .Resultado(\Saída [31]), .Vai_1(Overflow), .A(A31), .B(B31), .OperCode(OperCode));
  \Menu_de_Operações  \menu_de_operações_1  ();

  // Other names for the same wires on the sheet: S0 = \Saída [0]; S1 = \Saída [1]; S2 = \Saída [2]; S3 = \Saída [3];
  //   S4 = \Saída [4]; S5 = \Saída [5]; S6 = \Saída [6]; S7 = \Saída [7]; S8 = \Saída [8]; S9 = \Saída [9];
  //   S10 = \Saída [10]; S11 = \Saída [11]; S12 = \Saída [12]; S13 = \Saída [13]; S14 = \Saída [14];
  //   S15 = \Saída [15]; S16 = \Saída [16]; S17 = \Saída [17]; S18 = \Saída [18]; S19 = \Saída [19];
  //   S20 = \Saída [20]; S21 = \Saída [21]; S22 = \Saída [22]; S23 = \Saída [23]; S24 = \Saída [24];
  //   S25 = \Saída [25]; S26 = \Saída [26]; S27 = \Saída [27]; S28 = \Saída [28]; S29 = \Saída [29];
  //   S30 = \Saída [30]; S31 = \Saída [31]
endmodule

// SRL
module \Shift_Right_Logical__Deslocar_à_Direita  (
  input  [31:0] Entrada,
  input  OperCode,
  output [31:0] \Saída 
);

  Multiplexer #(.width(32), .enable("false")) multiplexer_1 (
    .in0(Entrada), .in1({1'b0, Entrada[31:1]}), .out(\Saída ), .sel(OperCode));
endmodule

// SLL
module \Shift_Left_Logical__Deslocar_à_Esquerda  (
  input  [31:0] Entrada,
  input  OperCode,
  output [31:0] \Saída 
);

  Multiplexer #(.width(32), .enable("false")) multiplexer_1 (
    .in0(Entrada), .in1({Entrada[30:0], 1'b0}), .out(\Saída ), .sel(OperCode));
endmodule

// SRA
module \Shift_Right_Arithmetic__Deslocamento_Aritmético_à_Direita  (
  input  [31:0] Entrada,
  input  OperCode,
  output [31:0] \Saída 
);

  Multiplexer #(.width(32), .enable("false")) multiplexer_1 (
    .in0(Entrada), .in1({{2{Entrada[31]}}, Entrada[30:1]}), .out(\Saída ), .sel(OperCode));
endmodule

// LUA
module \Operação_LUA  (
  input  [31:0] Entrada,
  input  OperCode,
  output [31:0] \Saída 
);

  Multiplexer #(.width(32), .enable("false")) multiplexer_1 (
    .in0(Entrada), .in1({Entrada[16:0], {15{1'b0}}}), .out(\Saída ), .sel(OperCode));
endmodule

module SRL_Detect (
  input  [4:0] OperCode,
  output \Saída 
);

  and and_1 (\Saída , ~OperCode[4], ~OperCode[3], OperCode[2], ~OperCode[1], ~OperCode[0]);  // AND_Gate
endmodule

module SLL_Detect (
  input  [4:0] OperCode,
  output \Saída 
);

  and and_1 (\Saída , ~OperCode[4], ~OperCode[3], OperCode[2], ~OperCode[1], OperCode[0]);  // AND_Gate
endmodule

module SRA_Detect (
  input  [4:0] OperCode,
  output \Saída 
);

  and and_1 (\Saída , ~OperCode[4], ~OperCode[3], OperCode[2], OperCode[1], ~OperCode[0]);  // AND_Gate
endmodule

module LUA_Detect (
  input  [4:0] OperCode,
  output \Saída 
);

  and and_1 (\Saída , ~OperCode[4], ~OperCode[3], OperCode[2], OperCode[1], OperCode[0]);  // AND_Gate
endmodule

module Registrador (
  input  [31:0] Entrada,
  input  CLK,
  input  Reset,
  output [31:0] \Saída 
);

  D_Flip_Flop d_ff_1 (.clk(CLK), .D(Entrada[0]), .Q(\Saída [0]), .reset(Reset));  // open: Qn, preset, en
  D_Flip_Flop d_ff_2 (.clk(CLK), .D(Entrada[16]), .Q(\Saída [16]), .reset(Reset));  // open: Qn, preset, en
  D_Flip_Flop d_ff_3 (.clk(CLK), .D(Entrada[1]), .Q(\Saída [1]), .reset(Reset));  // open: Qn, preset, en
  D_Flip_Flop d_ff_4 (.clk(CLK), .D(Entrada[17]), .Q(\Saída [17]), .reset(Reset));  // open: Qn, preset, en
  D_Flip_Flop d_ff_5 (.clk(CLK), .D(Entrada[2]), .Q(\Saída [2]), .reset(Reset));  // open: Qn, preset, en
  D_Flip_Flop d_ff_6 (.clk(CLK), .D(Entrada[18]), .Q(\Saída [18]), .reset(Reset));  // open: Qn, preset, en
  D_Flip_Flop d_ff_7 (.clk(CLK), .D(Entrada[3]), .Q(\Saída [3]), .reset(Reset));  // open: Qn, preset, en
  D_Flip_Flop d_ff_8 (.clk(CLK), .D(Entrada[19]), .Q(\Saída [19]), .reset(Reset));  // open: Qn, preset, en
  D_Flip_Flop d_ff_9 (.clk(CLK), .D(Entrada[4]), .Q(\Saída [4]), .reset(Reset));  // open: Qn, preset, en
  D_Flip_Flop d_ff_10 (.clk(CLK), .D(Entrada[20]), .Q(\Saída [20]), .reset(Reset));  // open: Qn, preset, en
  D_Flip_Flop d_ff_11 (.clk(CLK), .D(Entrada[5]), .Q(\Saída [5]), .reset(Reset));  // open: Qn, preset, en
  D_Flip_Flop d_ff_12 (.clk(CLK), .D(Entrada[21]), .Q(\Saída [21]), .reset(Reset));  // open: Qn, preset, en
  D_Flip_Flop d_ff_13 (.clk(CLK), .D(Entrada[6]), .Q(\Saída [6]), .reset(Reset));  // open: Qn, preset, en
  D_Flip_Flop d_ff_14 (.clk(CLK), .D(Entrada[22]), .Q(\Saída [22]), .reset(Reset));  // open: Qn, preset, en
  D_Flip_Flop d_ff_15 (.clk(CLK), .D(Entrada[7]), .Q(\Saída [7]), .reset(Reset));  // open: Qn, preset, en
  D_Flip_Flop d_ff_16 (.clk(CLK), .D(Entrada[23]), .Q(\Saída [23]), .reset(Reset));  // open: Qn, preset, en
  D_Flip_Flop d_ff_17 (.clk(CLK), .D(Entrada[8]), .Q(\Saída [8]), .reset(Reset));  // open: Qn, preset, en
  D_Flip_Flop d_ff_18 (.clk(CLK), .D(Entrada[24]), .Q(\Saída [24]), .reset(Reset));  // open: Qn, preset, en
  D_Flip_Flop d_ff_19 (.clk(CLK), .D(Entrada[9]), .Q(\Saída [9]), .reset(Reset));  // open: Qn, preset, en
  D_Flip_Flop d_ff_20 (.clk(CLK), .D(Entrada[25]), .Q(\Saída [25]), .reset(Reset));  // open: Qn, preset, en
  D_Flip_Flop d_ff_21 (.clk(CLK), .D(Entrada[10]), .Q(\Saída [10]), .reset(Reset));  // open: Qn, preset, en
  D_Flip_Flop d_ff_22 (.clk(CLK), .D(Entrada[26]), .Q(\Saída [26]), .reset(Reset));  // open: Qn, preset, en
  D_Flip_Flop d_ff_23 (.clk(CLK), .D(Entrada[11]), .Q(\Saída [11]), .reset(Reset));  // open: Qn, preset, en
  D_Flip_Flop d_ff_24 (.clk(CLK), .D(Entrada[27]), .Q(\Saída [27]), .reset(Reset));  // open: Qn, preset, en
  D_Flip_Flop d_ff_25 (.clk(CLK), .D(Entrada[12]), .Q(\Saída [12]), .reset(Reset));  // open: Qn, preset, en
  D_Flip_Flop d_ff_26 (.clk(CLK), .D(Entrada[28]), .Q(\Saída [28]), .reset(Reset));  // open: Qn, preset, en
  D_Flip_Flop d_ff_27 (.clk(CLK), .D(Entrada[13]), .Q(\Saída [13]), .reset(Reset));  // open: Qn, preset, en
  D_Flip_Flop d_ff_28 (.clk(CLK), .D(Entrada[29]), .Q(\Saída [29]), .reset(Reset));  // open: Qn, preset, en
  D_Flip_Flop d_ff_29 (.clk(CLK), .D(Entrada[14]), .Q(\Saída [14]), .reset(Reset));  // open: Qn, preset, en
  D_Flip_Flop d_ff_30 (.clk(CLK), .D(Entrada[30]), .Q(\Saída [30]), .reset(Reset));  // open: Qn, preset, en
  D_Flip_Flop d_ff_31 (.clk(CLK), .D(Entrada[15]), .Q(\Saída [15]), .reset(Reset));  // open: Qn, preset, en
  D_Flip_Flop d_ff_32 (.clk(CLK), .D(Entrada[31]), .Q(\Saída [31]), .reset(Reset));  // open: Qn, preset, en

  // Other names for the same wires on the sheet: E0 = Entrada[0]; E1 = Entrada[1]; E2 = Entrada[2]; E3 = Entrada[3];
  //   E4 = Entrada[4]; E5 = Entrada[5]; E6 = Entrada[6]; E7 = Entrada[7]; E8 = Entrada[8]; E9 = Entrada[9];
  //   E10 = Entrada[10]; E11 = Entrada[11]; E12 = Entrada[12]; E13 = Entrada[13]; E14 = Entrada[14];
  //   E15 = Entrada[15]; E16 = Entrada[16]; E17 = Entrada[17]; E18 = Entrada[18]; E19 = Entrada[19];
  //   E20 = Entrada[20]; E21 = Entrada[21]; E22 = Entrada[22]; E23 = Entrada[23]; E24 = Entrada[24];
  //   E25 = Entrada[25]; E26 = Entrada[26]; E27 = Entrada[27]; E28 = Entrada[28]; E29 = Entrada[29];
  //   E30 = Entrada[30]; E31 = Entrada[31]; S0 = \Saída [0]; S1 = \Saída [1]; S2 = \Saída [2]; S3 = \Saída [3];
  //   S4 = \Saída [4]; S5 = \Saída [5]; S6 = \Saída [6]; S7 = \Saída [7]; S8 = \Saída [8]; S9 = \Saída [9];
  //   S10 = \Saída [10]; S11 = \Saída [11]; S12 = \Saída [12]; S13 = \Saída [13]; S14 = \Saída [14];
  //   S15 = \Saída [15]; S16 = \Saída [16]; S17 = \Saída [17]; S18 = \Saída [18]; S19 = \Saída [19];
  //   S20 = \Saída [20]; S21 = \Saída [21]; S22 = \Saída [22]; S23 = \Saída [23]; S24 = \Saída [24];
  //   S25 = \Saída [25]; S26 = \Saída [26]; S27 = \Saída [27]; S28 = \Saída [28]; S29 = \Saída [29];
  //   S30 = \Saída [30]; S31 = \Saída [31]
endmodule

module Banco_de_Registradores (
  input  RESET,
  input  [31:0] DataIN,
  input  [4:0] SelRegA,
  input  [4:0] SelRegB,
  input  CLK,
  input  [4:0] SelRegCLK,
  output [31:0] DataRegA,
  output [31:0] DataRegB
);

  wire CLK_0, CLK_1, CLK_2, CLK_3, CLK_4, CLK_5, CLK_6, CLK_7, CLK_8, CLK_9, CLK_10, CLK_11, CLK_12, CLK_13,
       CLK_14, CLK_15, CLK_16, CLK_17, CLK_18, CLK_19, CLK_20, CLK_21, CLK_22, CLK_23, CLK_24, CLK_25,
       CLK_26, CLK_27, CLK_28, CLK_29, CLK_30, CLK_31;
  wire [31:0] S0, S1, S2, S3, S4, S5, S6, S7, S8, S9, S10, S11, S12, S13, S14, S15, S16, S17, S18, S19, S20,
       S21, S22, S23, S24, S25, S26, S27, S28, S29, S30, S31;

  Registrador _0 (.CLK(CLK_0), .Entrada({32{1'b0}}), .\Saída (S0), .Reset(RESET));
  Registrador _1 (.CLK(CLK_1), .Entrada(DataIN), .\Saída (S1), .Reset(RESET));
  Registrador _2 (.CLK(CLK_2), .Entrada(DataIN), .\Saída (S2), .Reset(RESET));
  Registrador _3 (.CLK(CLK_3), .Entrada(DataIN), .\Saída (S3), .Reset(RESET));
  Registrador _4 (.CLK(CLK_4), .Entrada(DataIN), .\Saída (S4), .Reset(RESET));
  Registrador _5 (.CLK(CLK_5), .Entrada(DataIN), .\Saída (S5), .Reset(RESET));
  Registrador _6 (.CLK(CLK_6), .Entrada(DataIN), .\Saída (S6), .Reset(RESET));
  Registrador _7 (.CLK(CLK_7), .Entrada(DataIN), .\Saída (S7), .Reset(RESET));
  Registrador _8 (.CLK(CLK_8), .Entrada(DataIN), .\Saída (S8), .Reset(RESET));
  Registrador _9 (.CLK(CLK_9), .Entrada(DataIN), .\Saída (S9), .Reset(RESET));
  Registrador _10 (.CLK(CLK_10), .Entrada(DataIN), .\Saída (S10), .Reset(RESET));
  Registrador _11 (.CLK(CLK_11), .Entrada(DataIN), .\Saída (S11), .Reset(RESET));
  Registrador _12 (.CLK(CLK_12), .Entrada(DataIN), .\Saída (S12), .Reset(RESET));
  Registrador _13 (.CLK(CLK_13), .Entrada(DataIN), .\Saída (S13), .Reset(RESET));
  Registrador _14 (.CLK(CLK_14), .Entrada(DataIN), .\Saída (S14), .Reset(RESET));
  Registrador _15 (.CLK(CLK_15), .Entrada(DataIN), .\Saída (S15), .Reset(RESET));
  Registrador _16 (.CLK(CLK_16), .Entrada(DataIN), .\Saída (S16), .Reset(RESET));
  Registrador _17 (.CLK(CLK_17), .Entrada(DataIN), .\Saída (S17), .Reset(RESET));
  Registrador _18 (.CLK(CLK_18), .Entrada(DataIN), .\Saída (S18), .Reset(RESET));
  Registrador _19 (.CLK(CLK_19), .Entrada(DataIN), .\Saída (S19), .Reset(RESET));
  Registrador _20 (.CLK(CLK_20), .Entrada(DataIN), .\Saída (S20), .Reset(RESET));
  Registrador _21 (.CLK(CLK_21), .Entrada(DataIN), .\Saída (S21), .Reset(RESET));
  Registrador _22 (.CLK(CLK_22), .Entrada(DataIN), .\Saída (S22), .Reset(RESET));
  Registrador _23 (.CLK(CLK_23), .Entrada(DataIN), .\Saída (S23), .Reset(RESET));
  Registrador _24 (.CLK(CLK_24), .Entrada(DataIN), .\Saída (S24), .Reset(RESET));
  Registrador _25 (.CLK(CLK_25), .Entrada(DataIN), .\Saída (S25), .Reset(RESET));
  Registrador _26 (.CLK(CLK_26), .Entrada(DataIN), .\Saída (S26), .Reset(RESET));
  Registrador _27 (.CLK(CLK_27), .Entrada(DataIN), .\Saída (S27), .Reset(RESET));
  Registrador _28 (.CLK(CLK_28), .Entrada(DataIN), .\Saída (S28), .Reset(RESET));
  Registrador _29 (.CLK(CLK_29), .Entrada(DataIN), .\Saída (S29), .Reset(RESET));
  Registrador _30 (.CLK(CLK_30), .Entrada(DataIN), .\Saída (S30), .Reset(RESET));
  Registrador _31 (.CLK(CLK_31), .Entrada(DataIN), .\Saída (S31), .Reset(RESET));
  Multiplexer #(.select(5), .width(32), .enable("false")) multiplexer_1 (
    .in0(S0), .in1(S1), .in2(S2), .in3(S3), .in4(S4), .in5(S5), .in6(S6), .in7(S7), .in8(S8), .in9(S9),
    .in10(S10), .in11(S11), .in12(S12), .in13(S13), .in14(S14), .in15(S15), .in16(S16), .in17(S17),
    .in18(S18), .in19(S19), .in20(S20), .in21(S21), .in22(S22), .in23(S23), .in24(S24), .in25(S25),
    .in26(S26), .in27(S27), .in28(S28), .in29(S29), .in30(S30), .in31(S31), .out(DataRegA), .sel(SelRegA));
  Multiplexer #(.select(5), .width(32), .enable("false")) multiplexer_2 (
    .in0(S0), .in1(S1), .in2(S2), .in3(S3), .in4(S4), .in5(S5), .in6(S6), .in7(S7), .in8(S8), .in9(S9),
    .in10(S10), .in11(S11), .in12(S12), .in13(S13), .in14(S14), .in15(S15), .in16(S16), .in17(S17),
    .in18(S18), .in19(S19), .in20(S20), .in21(S21), .in22(S22), .in23(S23), .in24(S24), .in25(S25),
    .in26(S26), .in27(S27), .in28(S28), .in29(S29), .in30(S30), .in31(S31), .out(DataRegB), .sel(SelRegB));
  Demultiplexer #(.select(5), .enable("false")) demultiplexer_1 (
    .out0(CLK_0), .out1(CLK_1), .out2(CLK_2), .out3(CLK_3), .out4(CLK_4), .out5(CLK_5), .out6(CLK_6),
    .out7(CLK_7), .out8(CLK_8), .out9(CLK_9), .out10(CLK_10), .out11(CLK_11), .out12(CLK_12), .out13(CLK_13),
    .out14(CLK_14), .out15(CLK_15), .out16(CLK_16), .out17(CLK_17), .out18(CLK_18), .out19(CLK_19),
    .out20(CLK_20), .out21(CLK_21), .out22(CLK_22), .out23(CLK_23), .out24(CLK_24), .out25(CLK_25),
    .out26(CLK_26), .out27(CLK_27), .out28(CLK_28), .out29(CLK_29), .out30(CLK_30), .out31(CLK_31), .in(CLK),
    .sel(SelRegCLK));
endmodule

module Via_de_Dados (
  input  CLK,
  input  Reset,
  input  [31:0] \Instrução ,
  output [7:0] Addr
);

  wire not_1_out, \ula_32_bits_2_números_1_overflow ;
  wire [31:0] banco_de_registradores_1_datarega, banco_de_registradores_1_dataregb, multiplexer_1_out,
       \n16_para_32_1_saída_32 , \ula_32_bits_2_números_1_saída ;

  not not_1 (not_1_out, CLK);
  PC pc_1 (.CLK(not_1_out), .RESET(Reset), .Addr(Addr));
  Banco_de_Registradores banco_de_registradores_1 (
    .DataRegA(banco_de_registradores_1_datarega), .DataRegB(banco_de_registradores_1_dataregb), .CLK(CLK),
    .DataIN(\ula_32_bits_2_números_1_saída ), .SelRegA(\Instrução [21:17]), .SelRegB(\Instrução [16:12]),
    .SelRegCLK(\Instrução [26:22]), .RESET(Reset));
  _16_para_32 u_16_para_32_1 (.Entrada_16(\Instrução [16:1]), .\Saída_32 (\n16_para_32_1_saída_32 ));
  LED Overflow (.in(\ula_32_bits_2_números_1_overflow ));
  Multiplexer #(.width(32), .enable("false")) multiplexer_1 (
    .in0(banco_de_registradores_1_dataregb), .in1(\n16_para_32_1_saída_32 ), .out(multiplexer_1_out),
    .sel(\Instrução [0]));
  \Menu_de_Instruções  \menu_de_instruções_1  ();
  \ULA___32_Bits__2_Números  \ula_32_bits_2_números_1  (
    .A(banco_de_registradores_1_datarega), .B(multiplexer_1_out), .\Saída (\ula_32_bits_2_números_1_saída ),
    .OperCode(\Instrução [31:27]), .Overflow(\ula_32_bits_2_números_1_overflow ), .SA(\Instrução [11:7]));
  \Menu_de_Operações  \menu_de_operações_1  ();

  // Other names for the same wires on the sheet: i = \Instrução [0]; Externo__11_Bits[10:0] = \Instrução [11:1];
  //   SelRegB[4:0] = \Instrução [16:12]; SelRegA[4:0] = \Instrução [21:17]; SelRegCLK[4:0] = \Instrução [26:22];
  //   SelOperCode[4:0] = \Instrução [31:27]; SA[4:0] = \Instrução [11:7]
endmodule

module _16_para_32 (
  input  [15:0] Entrada_16,
  output [31:0] \Saída_32 
);


  assign \Saída_32  = {{17{Entrada_16[15]}}, Entrada_16[14:0]};
endmodule

module PC (
  input  CLK,
  input  RESET,
  output [7:0] Addr
);

  wire [7:0] adder_1_out;

  Adder adder_1 (.a(Addr), .b(8'h1), .out(adder_1_out));  // open: cin, cout
  Register register_1 (.D(adder_1_out), .Q(Addr), .clk(CLK), .clr(RESET));  // open: en
endmodule

module Computador (
);

  wire CLK_out, Reset;
  wire [7:0] Addr;
  wire [31:0] ram_1_data;

  Button CLK (.out(CLK_out));
  Button u_Reset (.out(Reset));
  Via_de_Dados via_de_dados_1 (.CLK(CLK_out), .Reset(Reset), .\Instrução (ram_1_data), .Addr(Addr));
  RAM #(.dataWidth(32)) ram_1 (.addr(Addr), .data(ram_1_data), .clr(Reset));  // open: sel, clk, ld
endmodule

module SLL___32 (
  input  [31:0] Entrada,
  input  SLL_Detect__New,
  input  [4:0] SA,
  output [31:0] \Saída 
);

  wire [31:0] multiplexer_1_out;

  Multiplexer #(.select(5), .width(32), .enable("false")) multiplexer_1 (
    .in0(Entrada), .in1({Entrada[30:0], 1'b0}), .in2({Entrada[29:0], 2'b00}), .in3({Entrada[28:0], 3'b000}),
    .in4({Entrada[27:0], 4'b0000}), .out(multiplexer_1_out), .sel(SA));  // open: in5, in6, in7, in8, in9, in10, in11, in12, in13, in14, in15, in16, in17, in18, in19, in20, in21, in22, in23, in24, in25, in26, in27, in28, in29, in30, in31
  Multiplexer #(.width(32), .enable("false")) multiplexer_2 (
    .in0(Entrada), .in1(multiplexer_1_out), .out(\Saída ), .sel(SLL_Detect__New));
endmodule

module SLL_32___Detect (
  input  [4:0] OperCode,
  output \Saída 
);

  and and_1 (\Saída , ~OperCode[4], OperCode[3], ~OperCode[2], ~OperCode[1], ~OperCode[0]);  // AND_Gate
endmodule
